// Logisim project Cpu_32bit_Pipelined.circ as structural Verilog
module main (
);

  wire A__B, A_B, A_B_U, clk, controlunti_alucontrol_1_j_type, controlunti_alucontrol_1_memr,
       controlunti_alucontrol_1_memw, controlunti_alucontrol_1_regw, controlunti_alucontrol_1_writeback,
       Ex_RegW, ExtOp, kill, Mem_RegW, MemR, MemW, not_1_out, not_2_out, not_3_out, or_1_out, PC_ctrl,
       register_14_q, register_15_q, register_16_q, stall, Wb_RegW, WriteBack;
  wire [1:0] AluSel, controlunti_alucontrol_1_alusel, FwdA, FwdB, ImmSel;
  wire [3:0] AluOp, controlunti_alucontrol_1_aluop;
  wire [4:0] Ex_rd, imm15, imm20, Mem_rd, rd_imm5, Wb_rd;
  wire [6:0] multiplexer_3_out, Op;
  wire [7:0] PCSignals, register_1_q;
  wire [9:0] f_imm10;
  wire [25:0] D_PC, D_PC_4, Ex_PC, Ex_PC_4, multiplexer_1_out, PC, PC_4, target;
  wire [31:0] AluOut, bit_extender_1_out, BusA, BusB, BusW, Ex_BusA, Ex_BusB, Ex_ImmOut, ImmOut, Mem_AluOut,
       Mem_BusB, MemoryOut, multiplexer_2_out, multiplexer_6_out, ram_1_data, registerfile_1_busa,
       registerfile_1_busb, rom_1_data, shifter_1_out, shifter_2_out;

  Clock clock_1 (.out(clk));
  Register register_1 (.D(PCSignals), .Q(register_1_q), .clk(clk));  // open: en, clr
  Multiplexer #(.width(26), .enable("false")) multiplexer_1 (
    .in0(PC_4), .in1(target), .out(multiplexer_1_out), .sel(PC_ctrl));
  Register #(.width(26)) register_2 (.D(multiplexer_1_out), .en(not_1_out), .Q(PC), .clk(clk));  // open: clr
  not not_1 (not_1_out, stall);
  Adder #(.width(26)) adder_1 (.a(26'h4), .b(PC), .out(PC_4));  // open: cin, cout
  PCControl pccontrol_1 (
    .PCSignals(register_1_q), .A__B(A__B), .A_B(A_B), .A_B_u(A_B_U), .PC_ctrl(PC_ctrl), .kill(kill));
  ROM #(.addrWidth(24), .dataWidth(32)) rom_1 (.addr(PC[25:2]), .data(rom_1_data));  // open: sel
  Multiplexer #(.width(32), .enable("false")) multiplexer_2 (
    .in0(rom_1_data), .in1({32{1'b0}}), .out(multiplexer_2_out), .sel(kill));
  Register #(.width(26)) register_3 (.D(PC), .en(not_2_out), .Q(D_PC), .clk(clk));  // open: clr
  Register #(.width(26)) register_4 (.D(PC_4), .en(not_2_out), .Q(D_PC_4), .clk(clk));  // open: clr
  not not_2 (not_2_out, stall);
  Register #(.width(32)) register_5 (
    .D(multiplexer_2_out), .en(not_3_out), .Q({f_imm10, imm15, imm20, rd_imm5, Op}), .clk(clk));  // open: clr
  not not_3 (not_3_out, stall);
  Forwarding forwarding_1 (
    .rs1(imm20), .rs2(imm15), .Ex_rd(Ex_rd), .Mem_rd(Mem_rd), .Wb_rd(Wb_rd), .FwdA(FwdA), .stall(stall),
    .FwdB(FwdB), .Ex_RegW(Ex_RegW), .Mem_RegW(Mem_RegW), .Wb_RegW(Wb_RegW), .MemR(MemR),
    .j_type(controlunti_alucontrol_1_j_type));
  Multiplexer #(.width(7), .enable("false")) multiplexer_3 (
    .in0(Op), .in1({7{1'b0}}), .out(multiplexer_3_out), .sel(or_1_out));
  or or_1 (or_1_out, kill, stall);
  ControlUnti_AluControl controlunti_alucontrol_1 (
    .op(multiplexer_3_out), .f(f_imm10), .MemW(controlunti_alucontrol_1_memw),
    .MemR(controlunti_alucontrol_1_memr), .ExtOp(ExtOp), .WriteBack(controlunti_alucontrol_1_writeback),
    .RegW(controlunti_alucontrol_1_regw), .AluOp(controlunti_alucontrol_1_aluop),
    .AluSel(controlunti_alucontrol_1_alusel), .ImmSel(ImmSel), .PCSignals(PCSignals),
    .j_type(controlunti_alucontrol_1_j_type));
  ImmExtender immextender_1 (
    .imm15({f_imm10, imm15}), .imm10_imm5({f_imm10, rd_imm5}), .imm20({f_imm10, imm15, imm20}),
    .ImmOut(ImmOut), .ExtOp(ExtOp), .ImmSel(ImmSel));
  RegisterFile registerfile_1 (
    .RB(imm15), .RA(imm20), .RW(Wb_rd), .BusA(registerfile_1_busa), .BusB(registerfile_1_busb),
    .RegWrite(Wb_RegW), .BusW(BusW), .clk(clk));
  Multiplexer #(.select(2), .width(32), .enable("false")) multiplexer_4 (
    .in0(registerfile_1_busa), .in1(AluOut), .in2(MemoryOut), .in3(BusW), .out(BusA), .sel(FwdA));
  Multiplexer #(.select(2), .width(32), .enable("false")) multiplexer_5 (
    .in0(registerfile_1_busb), .in1(AluOut), .in2(MemoryOut), .in3(BusW), .out(BusB), .sel(FwdB));
  Register #(.width(26)) register_6 (.D(D_PC), .Q(Ex_PC), .clk(clk));  // open: en, clr
  Register #(.width(26)) register_7 (.D(D_PC_4), .Q(Ex_PC_4), .clk(clk));  // open: en, clr
  Register #(.width(32)) register_8 (.D(ImmOut), .Q(Ex_ImmOut), .clk(clk));  // open: en, clr
  Register #(.width(32)) register_9 (.D(BusA), .Q(Ex_BusA), .clk(clk));  // open: en, clr
  Register #(.width(32)) register_10 (.D(BusB), .Q(Ex_BusB), .clk(clk));  // open: en, clr
  Register #(.width(5)) register_11 (.D(rd_imm5), .Q(Ex_rd), .clk(clk));  // open: en, clr
  Register #(.width(2)) register_12 (.D(controlunti_alucontrol_1_alusel), .Q(AluSel), .clk(clk));  // open: en, clr
  Register #(.width(4)) register_13 (.D(controlunti_alucontrol_1_aluop), .Q(AluOp), .clk(clk));  // open: en, clr
  Register #(.width(1)) register_14 (.D(controlunti_alucontrol_1_memw), .Q(register_14_q), .clk(clk));  // open: en, clr
  Register #(.width(1)) register_15 (.D(controlunti_alucontrol_1_memr), .Q(register_15_q), .clk(clk));  // open: en, clr
  Register #(.width(1)) register_16 (
    .D(controlunti_alucontrol_1_writeback), .Q(register_16_q), .clk(clk));  // open: en, clr
  Register #(.width(1)) register_17 (.D(controlunti_alucontrol_1_regw), .Q(Ex_RegW), .clk(clk));  // open: en, clr
  Shifter #(.width(32)) shifter_1 (.in(Ex_ImmOut), .\dist (5'b01100), .out(shifter_1_out));
  assign bit_extender_1_out = {{6{1'b0}}, Ex_PC_4};  // Bit_Extender bit_extender_1
  Multiplexer #(.select(2), .width(32), .enable("false")) multiplexer_6 (
    .in0(Ex_BusB), .in1(Ex_ImmOut), .in2(shifter_1_out), .in3(bit_extender_1_out), .out(multiplexer_6_out),
    .sel(AluSel));
  Shifter #(.width(32)) shifter_2 (.in(Ex_ImmOut), .\dist (5'b00010), .out(shifter_2_out));
  Adder #(.width(26)) adder_2 (.a(Ex_PC), .b(shifter_2_out[25:0]), .out(target));  // open: cin, cout
  ALU alu_1 (.A(Ex_BusA), .B(multiplexer_6_out), .AluOut(AluOut), .AluOp(AluOp), .a__b(A__B), .a_b(A_B), .a_b_u(A_B_U));
  Register #(.width(32)) register_18 (.D(Ex_BusB), .Q(Mem_BusB), .clk(clk));  // open: en, clr
  Register #(.width(32)) register_19 (.D(AluOut), .Q(Mem_AluOut), .clk(clk));  // open: en, clr
  Register #(.width(5)) register_20 (.D(Ex_rd), .Q(Mem_rd), .clk(clk));  // open: en, clr
  Register #(.width(1)) register_21 (.D(register_14_q), .Q(MemW), .clk(clk));  // open: en, clr
  Register #(.width(1)) register_22 (.D(register_15_q), .Q(MemR), .clk(clk));  // open: en, clr
  Register #(.width(1)) register_23 (.D(register_16_q), .Q(WriteBack), .clk(clk));  // open: en, clr
  Register #(.width(1)) register_24 (.D(Ex_RegW), .Q(Mem_RegW), .clk(clk));  // open: en, clr
  RAM #(.addrWidth(24), .dataWidth(32), .bus("separate")) ram_1 (
    .addr(Mem_AluOut[25:2]), .din(Mem_BusB), .data(ram_1_data), .str(MemW), .clk(clk), .ld(MemR));  // open: sel, clr
  Multiplexer #(.width(32), .enable("false")) multiplexer_7 (
    .in0(Mem_AluOut), .in1(ram_1_data), .out(MemoryOut), .sel(WriteBack));
  Register #(.width(32)) register_25 (.D(MemoryOut), .Q(BusW), .clk(clk));  // open: en, clr
  Register #(.width(5)) register_26 (.D(Mem_rd), .Q(Wb_rd), .clk(clk));  // open: en, clr
  Register #(.width(1)) register_27 (.D(Mem_RegW), .Q(Wb_RegW), .clk(clk));  // open: en, clr

  // Other names for the same wires on the sheet: rs1[4:0] = imm20; imm20[19:5] = {f_imm10, imm15}; rs2[4:0] = imm15;
  //   imm15[14:5] = f_imm10

  // Notes on the sheet:
  //   Fetch
  //   contents of rom_1 (hex, n*v repeats v):
  //   80093 20023 40093 20223 c0093 20423 20093 20623 e0093 20823 413 a0493 5b3 fffe9513 1489e7 160633
  //   28693 8b713 12d467 c89c e91c 232167 1c0633 8e713 2d693 ffff906e cc1c bc9c 32c023 30b023 8b593 28413
  //   fffed06e 6e
  //   Decode
  //   Excute
  //   Memory
  //   WriteBack
endmodule

module RegisterFile (
  input  [4:0] RB,
  input  [4:0] RA,
  input  [4:0] RW,
  input  [31:0] BusW,
  input  clk,
  input  RegWrite,
  output [31:0] BusA,
  output [31:0] BusB
);

  wire and_1_out, and_2_out, and_3_out, and_4_out, and_5_out, and_6_out, and_7_out, and_8_out, and_9_out,
       and_10_out, and_11_out, and_12_out, and_13_out, and_14_out, and_15_out, and_16_out, and_17_out,
       and_18_out, and_19_out, and_20_out, and_21_out, and_22_out, and_23_out, and_24_out, and_25_out,
       and_26_out, and_27_out, and_28_out, and_29_out, and_30_out, and_31_out, decoder_1_out1,
       decoder_1_out2, decoder_1_out3, decoder_1_out4, decoder_1_out5, decoder_1_out6, decoder_1_out7,
       decoder_1_out8, decoder_1_out9, decoder_1_out10, decoder_1_out11, decoder_1_out12, decoder_1_out13,
       decoder_1_out14, decoder_1_out15, decoder_1_out16, decoder_1_out17, decoder_1_out18, decoder_1_out19,
       decoder_1_out20, decoder_1_out21, decoder_1_out22, decoder_1_out23, decoder_1_out24, decoder_1_out25,
       decoder_1_out26, decoder_1_out27, decoder_1_out28, decoder_1_out29, decoder_1_out30, decoder_1_out31,
       decoder_2_out0, decoder_2_out1, decoder_2_out2, decoder_2_out3, decoder_2_out4, decoder_2_out5,
       decoder_2_out6, decoder_2_out7, decoder_2_out8, decoder_2_out9, decoder_2_out10, decoder_2_out11,
       decoder_2_out12, decoder_2_out13, decoder_2_out14, decoder_2_out15, decoder_2_out16, decoder_2_out17,
       decoder_2_out18, decoder_2_out19, decoder_2_out20, decoder_2_out21, decoder_2_out22, decoder_2_out23,
       decoder_2_out24, decoder_2_out25, decoder_2_out26, decoder_2_out27, decoder_2_out28, decoder_2_out29,
       decoder_2_out30, decoder_2_out31, decoder_3_out0, decoder_3_out1, decoder_3_out2, decoder_3_out3,
       decoder_3_out4, decoder_3_out5, decoder_3_out6, decoder_3_out7, decoder_3_out8, decoder_3_out9,
       decoder_3_out10, decoder_3_out11, decoder_3_out12, decoder_3_out13, decoder_3_out14, decoder_3_out15,
       decoder_3_out16, decoder_3_out17, decoder_3_out18, decoder_3_out19, decoder_3_out20, decoder_3_out21,
       decoder_3_out22, decoder_3_out23, decoder_3_out24, decoder_3_out25, decoder_3_out26, decoder_3_out27,
       decoder_3_out28, decoder_3_out29, decoder_3_out30, decoder_3_out31;
  wire [31:0] R1_q, R2_q, R3_q, R4_q, R5_q, R6_q, R7_q, R8_q, R9_q, R10_q, R11_q, R12_q, R13_q, R14_q, R15_q,
       R16_q, R17_q, R18_q, R19_q, R20_q, R21_q, R22_q, R23_q, R24_q, R25_q, R26_q, R27_q, R28_q, R29_q,
       R30_q, R31_q;

  Decoder #(.select(5), .enable("false")) decoder_1 (
    .out1(decoder_1_out1), .out2(decoder_1_out2), .out3(decoder_1_out3), .out4(decoder_1_out4),
    .out5(decoder_1_out5), .out6(decoder_1_out6), .out7(decoder_1_out7), .out8(decoder_1_out8),
    .out9(decoder_1_out9), .out10(decoder_1_out10), .out11(decoder_1_out11), .out12(decoder_1_out12),
    .out13(decoder_1_out13), .out14(decoder_1_out14), .out15(decoder_1_out15), .out16(decoder_1_out16),
    .out17(decoder_1_out17), .out18(decoder_1_out18), .out19(decoder_1_out19), .out20(decoder_1_out20),
    .out21(decoder_1_out21), .out22(decoder_1_out22), .out23(decoder_1_out23), .out24(decoder_1_out24),
    .out25(decoder_1_out25), .out26(decoder_1_out26), .out27(decoder_1_out27), .out28(decoder_1_out28),
    .out29(decoder_1_out29), .out30(decoder_1_out30), .out31(decoder_1_out31), .sel(RW));  // open: out0
  and and_1 (and_1_out, decoder_1_out1, RegWrite);
  and and_2 (and_2_out, decoder_1_out2, RegWrite);
  and and_3 (and_3_out, decoder_1_out3, RegWrite);
  and and_4 (and_4_out, decoder_1_out4, RegWrite);
  and and_5 (and_5_out, decoder_1_out5, RegWrite);
  and and_6 (and_6_out, decoder_1_out6, RegWrite);
  and and_7 (and_7_out, decoder_1_out7, RegWrite);
  and and_8 (and_8_out, decoder_1_out8, RegWrite);
  and and_9 (and_9_out, decoder_1_out9, RegWrite);
  and and_10 (and_10_out, decoder_1_out10, RegWrite);
  and and_11 (and_11_out, decoder_1_out11, RegWrite);
  and and_12 (and_12_out, decoder_1_out12, RegWrite);
  and and_13 (and_13_out, decoder_1_out13, RegWrite);
  and and_14 (and_14_out, decoder_1_out14, RegWrite);
  and and_15 (and_15_out, decoder_1_out15, RegWrite);
  and and_16 (and_16_out, decoder_1_out16, RegWrite);
  and and_17 (and_17_out, decoder_1_out17, RegWrite);
  and and_18 (and_18_out, decoder_1_out18, RegWrite);
  and and_19 (and_19_out, decoder_1_out19, RegWrite);
  and and_20 (and_20_out, decoder_1_out20, RegWrite);
  and and_21 (and_21_out, decoder_1_out21, RegWrite);
  and and_22 (and_22_out, decoder_1_out22, RegWrite);
  and and_23 (and_23_out, decoder_1_out23, RegWrite);
  and and_24 (and_24_out, decoder_1_out24, RegWrite);
  and and_25 (and_25_out, decoder_1_out25, RegWrite);
  and and_26 (and_26_out, decoder_1_out26, RegWrite);
  and and_27 (and_27_out, decoder_1_out27, RegWrite);
  and and_28 (and_28_out, decoder_1_out28, RegWrite);
  and and_29 (and_29_out, decoder_1_out29, RegWrite);
  and and_30 (and_30_out, decoder_1_out30, RegWrite);
  and and_31 (and_31_out, decoder_1_out31, RegWrite);
  Decoder #(.select(5), .enable("false")) decoder_2 (
    .out0(decoder_2_out0), .out1(decoder_2_out1), .out2(decoder_2_out2), .out3(decoder_2_out3),
    .out4(decoder_2_out4), .out5(decoder_2_out5), .out6(decoder_2_out6), .out7(decoder_2_out7),
    .out8(decoder_2_out8), .out9(decoder_2_out9), .out10(decoder_2_out10), .out11(decoder_2_out11),
    .out12(decoder_2_out12), .out13(decoder_2_out13), .out14(decoder_2_out14), .out15(decoder_2_out15),
    .out16(decoder_2_out16), .out17(decoder_2_out17), .out18(decoder_2_out18), .out19(decoder_2_out19),
    .out20(decoder_2_out20), .out21(decoder_2_out21), .out22(decoder_2_out22), .out23(decoder_2_out23),
    .out24(decoder_2_out24), .out25(decoder_2_out25), .out26(decoder_2_out26), .out27(decoder_2_out27),
    .out28(decoder_2_out28), .out29(decoder_2_out29), .out30(decoder_2_out30), .out31(decoder_2_out31),
    .sel(RA));
  Register #(.width(32)) R1 (.D(BusW), .en(and_1_out), .Q(R1_q), .clk(clk));  // open: clr
  Register #(.width(32)) R2 (.D(BusW), .en(and_2_out), .Q(R2_q), .clk(clk));  // open: clr
  Register #(.width(32)) R3 (.D(BusW), .en(and_3_out), .Q(R3_q), .clk(clk));  // open: clr
  Register #(.width(32)) R4 (.en(and_4_out), .Q(R4_q));  // open: D, clk, clr
  Register #(.width(32)) R5 (.D(BusW), .en(and_5_out), .Q(R5_q), .clk(clk));  // open: clr
  Register #(.width(32)) R6 (.D(BusW), .en(and_6_out), .Q(R6_q), .clk(clk));  // open: clr
  Register #(.width(32)) R7 (.D(BusW), .en(and_7_out), .Q(R7_q), .clk(clk));  // open: clr
  Register #(.width(32)) R8 (.D(BusW), .en(and_8_out), .Q(R8_q), .clk(clk));  // open: clr
  Register #(.width(32)) R9 (.D(BusW), .en(and_9_out), .Q(R9_q), .clk(clk));  // open: clr
  Register #(.width(32)) R10 (.D(BusW), .en(and_10_out), .Q(R10_q), .clk(clk));  // open: clr
  Register #(.width(32)) R11 (.D(BusW), .en(and_11_out), .Q(R11_q), .clk(clk));  // open: clr
  Register #(.width(32)) R12 (.D(BusW), .en(and_12_out), .Q(R12_q), .clk(clk));  // open: clr
  Register #(.width(32)) R13 (.D(BusW), .en(and_13_out), .Q(R13_q), .clk(clk));  // open: clr
  Register #(.width(32)) R14 (.D(BusW), .en(and_14_out), .Q(R14_q), .clk(clk));  // open: clr
  Register #(.width(32)) R15 (.D(BusW), .en(and_15_out), .Q(R15_q), .clk(clk));  // open: clr
  Register #(.width(32)) R16 (.D(BusW), .en(and_16_out), .Q(R16_q), .clk(clk));  // open: clr
  Register #(.width(32)) R17 (.D(BusW), .en(and_17_out), .Q(R17_q), .clk(clk));  // open: clr
  Register #(.width(32)) R18 (.D(BusW), .en(and_18_out), .Q(R18_q), .clk(clk));  // open: clr
  Register #(.width(32)) R19 (.D(BusW), .en(and_19_out), .Q(R19_q), .clk(clk));  // open: clr
  Register #(.width(32)) R20 (.D(BusW), .en(and_20_out), .Q(R20_q), .clk(clk));  // open: clr
  Register #(.width(32)) R21 (.D(BusW), .en(and_21_out), .Q(R21_q), .clk(clk));  // open: clr
  Register #(.width(32)) R22 (.D(BusW), .en(and_22_out), .Q(R22_q), .clk(clk));  // open: clr
  Register #(.width(32)) R23 (.D(BusW), .en(and_23_out), .Q(R23_q), .clk(clk));  // open: clr
  Register #(.width(32)) R24 (.D(BusW), .en(and_24_out), .Q(R24_q), .clk(clk));  // open: clr
  Register #(.width(32)) R25 (.D(BusW), .en(and_25_out), .Q(R25_q), .clk(clk));  // open: clr
  Register #(.width(32)) R26 (.D(BusW), .en(and_26_out), .Q(R26_q), .clk(clk));  // open: clr
  Register #(.width(32)) R27 (.D(BusW), .en(and_27_out), .Q(R27_q), .clk(clk));  // open: clr
  Register #(.width(32)) R28 (.D(BusW), .en(and_28_out), .Q(R28_q), .clk(clk));  // open: clr
  Register #(.width(32)) R29 (.D(BusW), .en(and_29_out), .Q(R29_q), .clk(clk));  // open: clr
  Register #(.width(32)) R30 (.D(BusW), .en(and_30_out), .Q(R30_q), .clk(clk));  // open: clr
  Register #(.width(32)) R31 (.D(BusW), .en(and_31_out), .Q(R31_q), .clk(clk));  // open: clr
  assign BusA = decoder_2_out0 ? {32{1'b0}} : 32'bz;  // Controlled_Buffer controlled_buffer_1
  assign BusA = decoder_2_out1 ? R1_q : 32'bz;  // Controlled_Buffer controlled_buffer_2
  assign BusA = decoder_2_out2 ? R2_q : 32'bz;  // Controlled_Buffer controlled_buffer_3
  assign BusA = decoder_2_out3 ? R3_q : 32'bz;  // Controlled_Buffer controlled_buffer_4
  assign BusA = decoder_2_out4 ? R4_q : 32'bz;  // Controlled_Buffer controlled_buffer_5
  assign BusA = decoder_2_out5 ? R5_q : 32'bz;  // Controlled_Buffer controlled_buffer_6
  assign BusA = decoder_2_out6 ? R6_q : 32'bz;  // Controlled_Buffer controlled_buffer_7
  assign BusA = decoder_2_out7 ? R7_q : 32'bz;  // Controlled_Buffer controlled_buffer_8
  assign BusA = decoder_2_out8 ? R8_q : 32'bz;  // Controlled_Buffer controlled_buffer_9
  assign BusA = decoder_2_out9 ? R9_q : 32'bz;  // Controlled_Buffer controlled_buffer_10
  assign BusA = decoder_2_out10 ? R10_q : 32'bz;  // Controlled_Buffer controlled_buffer_11
  assign BusA = decoder_2_out11 ? R11_q : 32'bz;  // Controlled_Buffer controlled_buffer_12
  assign BusA = decoder_2_out12 ? R12_q : 32'bz;  // Controlled_Buffer controlled_buffer_13
  assign BusA = decoder_2_out13 ? R13_q : 32'bz;  // Controlled_Buffer controlled_buffer_14
  assign BusA = decoder_2_out14 ? R14_q : 32'bz;  // Controlled_Buffer controlled_buffer_15
  assign BusA = decoder_2_out15 ? R15_q : 32'bz;  // Controlled_Buffer controlled_buffer_16
  assign BusA = decoder_2_out16 ? R16_q : 32'bz;  // Controlled_Buffer controlled_buffer_17
  assign BusA = decoder_2_out17 ? R17_q : 32'bz;  // Controlled_Buffer controlled_buffer_18
  assign BusA = decoder_2_out18 ? R18_q : 32'bz;  // Controlled_Buffer controlled_buffer_19
  assign BusA = decoder_2_out19 ? R19_q : 32'bz;  // Controlled_Buffer controlled_buffer_20
  assign BusA = decoder_2_out20 ? R20_q : 32'bz;  // Controlled_Buffer controlled_buffer_21
  assign BusA = decoder_2_out21 ? R21_q : 32'bz;  // Controlled_Buffer controlled_buffer_22
  assign BusA = decoder_2_out22 ? R22_q : 32'bz;  // Controlled_Buffer controlled_buffer_23
  assign BusA = decoder_2_out23 ? R23_q : 32'bz;  // Controlled_Buffer controlled_buffer_24
  assign BusA = decoder_2_out24 ? R24_q : 32'bz;  // Controlled_Buffer controlled_buffer_25
  assign BusA = decoder_2_out25 ? R25_q : 32'bz;  // Controlled_Buffer controlled_buffer_26
  assign BusA = decoder_2_out26 ? R26_q : 32'bz;  // Controlled_Buffer controlled_buffer_27
  assign BusA = decoder_2_out27 ? R27_q : 32'bz;  // Controlled_Buffer controlled_buffer_28
  assign BusA = decoder_2_out28 ? R28_q : 32'bz;  // Controlled_Buffer controlled_buffer_29
  assign BusA = decoder_2_out29 ? R29_q : 32'bz;  // Controlled_Buffer controlled_buffer_30
  assign BusA = decoder_2_out30 ? R30_q : 32'bz;  // Controlled_Buffer controlled_buffer_31
  assign BusA = decoder_2_out31 ? R31_q : 32'bz;  // Controlled_Buffer controlled_buffer_32
  Decoder #(.select(5), .enable("false")) decoder_3 (
    .out0(decoder_3_out0), .out1(decoder_3_out1), .out2(decoder_3_out2), .out3(decoder_3_out3),
    .out4(decoder_3_out4), .out5(decoder_3_out5), .out6(decoder_3_out6), .out7(decoder_3_out7),
    .out8(decoder_3_out8), .out9(decoder_3_out9), .out10(decoder_3_out10), .out11(decoder_3_out11),
    .out12(decoder_3_out12), .out13(decoder_3_out13), .out14(decoder_3_out14), .out15(decoder_3_out15),
    .out16(decoder_3_out16), .out17(decoder_3_out17), .out18(decoder_3_out18), .out19(decoder_3_out19),
    .out20(decoder_3_out20), .out21(decoder_3_out21), .out22(decoder_3_out22), .out23(decoder_3_out23),
    .out24(decoder_3_out24), .out25(decoder_3_out25), .out26(decoder_3_out26), .out27(decoder_3_out27),
    .out28(decoder_3_out28), .out29(decoder_3_out29), .out30(decoder_3_out30), .out31(decoder_3_out31),
    .sel(RB));
  assign BusB = decoder_3_out0 ? {32{1'b0}} : 32'bz;  // Controlled_Buffer controlled_buffer_33
  assign BusB = decoder_3_out1 ? R1_q : 32'bz;  // Controlled_Buffer controlled_buffer_34
  assign BusB = decoder_3_out2 ? R2_q : 32'bz;  // Controlled_Buffer controlled_buffer_35
  assign BusB = decoder_3_out3 ? R3_q : 32'bz;  // Controlled_Buffer controlled_buffer_36
  assign BusB = decoder_3_out4 ? R4_q : 32'bz;  // Controlled_Buffer controlled_buffer_37
  assign BusB = decoder_3_out5 ? R5_q : 32'bz;  // Controlled_Buffer controlled_buffer_38
  assign BusB = decoder_3_out6 ? R6_q : 32'bz;  // Controlled_Buffer controlled_buffer_39
  assign BusB = decoder_3_out7 ? R7_q : 32'bz;  // Controlled_Buffer controlled_buffer_40
  assign BusB = decoder_3_out8 ? R8_q : 32'bz;  // Controlled_Buffer controlled_buffer_41
  assign BusB = decoder_3_out9 ? R9_q : 32'bz;  // Controlled_Buffer controlled_buffer_42
  assign BusB = decoder_3_out10 ? R10_q : 32'bz;  // Controlled_Buffer controlled_buffer_43
  assign BusB = decoder_3_out11 ? R11_q : 32'bz;  // Controlled_Buffer controlled_buffer_44
  assign BusB = decoder_3_out12 ? R12_q : 32'bz;  // Controlled_Buffer controlled_buffer_45
  assign BusB = decoder_3_out13 ? R13_q : 32'bz;  // Controlled_Buffer controlled_buffer_46
  assign BusB = decoder_3_out14 ? R14_q : 32'bz;  // Controlled_Buffer controlled_buffer_47
  assign BusB = decoder_3_out15 ? R15_q : 32'bz;  // Controlled_Buffer controlled_buffer_48
  assign BusB = decoder_3_out16 ? R16_q : 32'bz;  // Controlled_Buffer controlled_buffer_49
  assign BusB = decoder_3_out17 ? R17_q : 32'bz;  // Controlled_Buffer controlled_buffer_50
  assign BusB = decoder_3_out18 ? R18_q : 32'bz;  // Controlled_Buffer controlled_buffer_51
  assign BusB = decoder_3_out19 ? R19_q : 32'bz;  // Controlled_Buffer controlled_buffer_52
  assign BusB = decoder_3_out20 ? R20_q : 32'bz;  // Controlled_Buffer controlled_buffer_53
  assign BusB = decoder_3_out21 ? R21_q : 32'bz;  // Controlled_Buffer controlled_buffer_54
  assign BusB = decoder_3_out22 ? R22_q : 32'bz;  // Controlled_Buffer controlled_buffer_55
  assign BusB = decoder_3_out23 ? R23_q : 32'bz;  // Controlled_Buffer controlled_buffer_56
  assign BusB = decoder_3_out24 ? R24_q : 32'bz;  // Controlled_Buffer controlled_buffer_57
  assign BusB = decoder_3_out25 ? R25_q : 32'bz;  // Controlled_Buffer controlled_buffer_58
  assign BusB = decoder_3_out26 ? R26_q : 32'bz;  // Controlled_Buffer controlled_buffer_59
  assign BusB = decoder_3_out27 ? R27_q : 32'bz;  // Controlled_Buffer controlled_buffer_60
  assign BusB = decoder_3_out28 ? R28_q : 32'bz;  // Controlled_Buffer controlled_buffer_61
  assign BusB = decoder_3_out29 ? R29_q : 32'bz;  // Controlled_Buffer controlled_buffer_62
  assign BusB = decoder_3_out30 ? R30_q : 32'bz;  // Controlled_Buffer controlled_buffer_63
  assign BusB = decoder_3_out31 ? R31_q : 32'bz;  // Controlled_Buffer controlled_buffer_64
endmodule

module ImmExtender (
  input  [14:0] imm15,
  input  [14:0] imm10_imm5,
  input  [19:0] imm20,
  input  [1:0] ImmSel,
  input  ExtOp,
  output [31:0] ImmOut
);

  wire [31:0] bit_extender_1_out, bit_extender_2_out, bit_extender_3_out, bit_extender_4_out,
       bit_extender_5_out, bit_extender_6_out, multiplexer_1_out, multiplexer_2_out, multiplexer_3_out;

  assign bit_extender_1_out = {{17{1'b0}}, imm15};  // Bit_Extender bit_extender_1
  assign bit_extender_2_out = {{17{imm15[14]}}, imm15};  // Bit_Extender bit_extender_2
  assign bit_extender_3_out = {{17{1'b0}}, imm10_imm5};  // Bit_Extender bit_extender_3
  assign bit_extender_4_out = {{17{imm10_imm5[14]}}, imm10_imm5};  // Bit_Extender bit_extender_4
  assign bit_extender_5_out = {{12{1'b0}}, imm20};  // Bit_Extender bit_extender_5
  assign bit_extender_6_out = {{12{imm20[19]}}, imm20};  // Bit_Extender bit_extender_6
  Multiplexer #(.width(32), .enable("false")) multiplexer_1 (
    .in0(bit_extender_1_out), .in1(bit_extender_2_out), .out(multiplexer_1_out), .sel(ExtOp));
  Multiplexer #(.width(32), .enable("false")) multiplexer_2 (
    .in0(bit_extender_3_out), .in1(bit_extender_4_out), .out(multiplexer_2_out), .sel(ExtOp));
  Multiplexer #(.width(32), .enable("false")) multiplexer_3 (
    .in0(bit_extender_5_out), .in1(bit_extender_6_out), .out(multiplexer_3_out), .sel(ExtOp));
  Multiplexer #(.select(2), .width(32), .enable("false")) multiplexer_4 (
    .in0(multiplexer_1_out), .in1(multiplexer_2_out), .in2(multiplexer_3_out), .out(ImmOut), .sel(ImmSel));  // open: in3
endmodule

module ALU (
  input  [31:0] A,
  input  [31:0] B,
  input  [3:0] AluOp,
  output a__b,
  output a_b,
  output a_b_u,
  output [31:0] AluOut
);

  wire comparator_1_lt, comparator_2_lt;
  wire [31:0] adder_1_out, and_1_out, bit_extender_1_out, bit_extender_2_out, or_1_out, shifter_1_out,
       shifter_2_out, shifter_3_out, subtractor_1_out, xor_1_out;

  Adder #(.width(32)) adder_1 (.a(A), .b(B), .out(adder_1_out));  // open: cin, cout
  Subtractor #(.width(32)) subtractor_1 (.a(A), .b(B), .out(subtractor_1_out));  // open: bin, bout
  Comparator #(.width(32)) comparator_1 (.a(A), .b(B), .lt(comparator_1_lt));  // open: gt, eq
  Comparator #(.width(32), .mode("unsigned")) comparator_2 (.a(A), .b(B), .lt(comparator_2_lt));  // open: gt, eq
  assign xor_1_out = A ^ B;  // XOR_Gate xor_1, 32 bits wide
  assign or_1_out = A | B;  // OR_Gate or_1, 32 bits wide
  assign and_1_out = A & B;  // AND_Gate and_1, 32 bits wide
  Shifter #(.width(32)) shifter_1 (.in(A), .\dist (B[4:0]), .out(shifter_1_out));
  Shifter #(.width(32), .shift("lr")) shifter_2 (.in(A), .\dist (B[4:0]), .out(shifter_2_out));
  Shifter #(.width(32), .shift("ar")) shifter_3 (.in(A), .\dist (B[4:0]), .out(shifter_3_out));
  assign bit_extender_1_out = {{31{1'b0}}, comparator_1_lt};  // Bit_Extender bit_extender_1
  assign bit_extender_2_out = {{31{1'b0}}, comparator_2_lt};  // Bit_Extender bit_extender_2
  Multiplexer #(.select(4), .width(32), .enable("false")) multiplexer_1 (
    .in0(adder_1_out), .in1(subtractor_1_out), .in2(bit_extender_1_out), .in3(bit_extender_2_out),
    .in4(xor_1_out), .in5(or_1_out), .in6(and_1_out), .in7(shifter_1_out), .in8(shifter_2_out),
    .in9(shifter_3_out), .in10(B), .out(AluOut), .sel(AluOp));  // open: in11, in12, in13, in14, in15
  Comparator #(.width(32)) comparator_3 (.a(A), .b(B), .eq(a__b), .lt(a_b));  // open: gt
  Comparator #(.width(32), .mode("unsigned")) comparator_4 (.a(A), .b(B), .lt(a_b_u));  // open: gt, eq
endmodule

// ControlUnit
module ControlUnti_AluControl (
  input  [6:0] op,
  input  [9:0] f,
  output MemW,
  output MemR,
  output WriteBack,
  output ExtOp,
  output j_type,
  output RegW,
  output [3:0] AluOp,
  output [1:0] AluSel,
  output [7:0] PCSignals,
  output [1:0] ImmSel
);

  wire _0x6X, add, addi, \and , andi, decoder_1_out3, i_type, lui, nop, nor_1_out, nor_2_out, not_1_out,
       not_2_out, \or , or_2_out, or_3_out, or_4_out, or_5_out, or_6_out, or_7_out, or_8_out, or_9_out,
       or_10_out, or_11_out, or_12_out, or_13_out, or_14_out, or_15_out, or_16_out, or_17_out, ori, r_type,
       sll, slli, slt, slti, sltiu, sltu, sra, srai, srl, srli, sub, \xor , xori;

  Decoder #(.select(3), .enable("false")) decoder_1 (
    .out0(nop), .out1(i_type), .out2(MemW), .out3(decoder_1_out3), .out6(_0x6X), .sel(op[6:4]));  // open: out4, out5, out7
  Decoder #(.select(4), .disabled(0)) decoder_2 (
    .out3(addi), .out4(slti), .out5(sltiu), .out6(xori), .out7(ori), .out8(andi), .out9(slli), .out10(srli),
    .out11(srai), .out12(MemR), .sel(op[3:0]), .en(i_type));  // open: out0, out1, out2, out13, out14, out15
  Decoder #(.select(4), .disabled(0)) decoder_3 (
    .out0(add), .out1(sub), .out2(slt), .out3(sltu), .out4(\xor ), .out5(\or ), .out6(\and ), .out7(sll),
    .out8(srl), .out9(sra), .sel(f[3:0]), .en(r_type));  // open: out10, out11, out12, out13, out14, out15
  Decoder #(.select(4), .disabled(0)) decoder_4 (
    .out3(r_type), .out7(lui), .sel(op[3:0]), .en(decoder_1_out3));  // open: out0, out1, out2, out4, out5, out6, out8, out9, out10, out11, out12, out13, out14, out15
  Decoder #(.select(4), .disabled(0)) decoder_5 (
    .out4(PCSignals[7]), .out5(PCSignals[6]), .out6(PCSignals[5]), .out7(PCSignals[4]), .out8(PCSignals[3]),
    .out9(PCSignals[2]), .out14(PCSignals[1]), .out15(PCSignals[0]), .sel(op[3:0]), .en(_0x6X));  // open: out0, out1, out2, out3, out10, out11, out12, out13
  or or_1 (j_type, lui, PCSignals[1]);
  not not_1 (not_1_out, nop);
  or or_2 (or_2_out, lui, PCSignals[1], PCSignals[0]);
  nor nor_1 (nor_1_out, MemW, PCSignals[7], PCSignals[6], PCSignals[5], PCSignals[4], PCSignals[3], PCSignals[2]);
  or or_3 (or_3_out, sra, srli);
  and and_1 (RegW, nor_1_out, not_1_out);
  or or_4 (or_4_out, srl, srli);
  or or_5 (or_5_out, PCSignals[1], PCSignals[0]);
  or or_6 (or_6_out, PCSignals[1], lui);
  or or_7 (or_7_out, sll, slli);
  or or_8 (or_8_out, \and , andi);
  or or_9 (or_9_out, MemW, i_type);
  or or_10 (or_10_out, PCSignals[7], PCSignals[6], PCSignals[5], PCSignals[4], PCSignals[3], PCSignals[2], MemW);
  or or_11 (or_11_out, \or , ori);
  or or_12 (or_12_out, PCSignals[7], PCSignals[6], PCSignals[5], PCSignals[4], PCSignals[3], PCSignals[2], r_type);
  or or_13 (or_13_out, \xor , xori);
  Priority_Encoder #(.select(2)) priority_encoder_1 (
    .in0(or_12_out), .in1(or_9_out), .in2(lui), .in3(or_5_out), .out(AluSel));  // open: gs, en_out, en_in
  or or_14 (or_14_out, PCSignals[0], i_type);
  not not_2 (not_2_out, nop);
  or or_15 (or_15_out, sltu, sltiu);
  or or_16 (or_16_out, slt, slti);
  Priority_Encoder #(.select(2)) priority_encoder_2 (
    .in0(or_14_out), .in1(or_10_out), .in2(or_6_out), .out(ImmSel));  // open: in3, gs, en_out, en_in
  nor nor_2 (nor_2_out, xori, ori, andi);
  and and_2 (ExtOp, nor_2_out, not_2_out);
  or or_17 (or_17_out, add, addi, MemW, MemR);
  Priority_Encoder #(.select(4)) priority_encoder_3 (
    .in0(or_17_out), .in1(sub), .in2(or_16_out), .in3(or_15_out), .in4(or_13_out), .in5(or_11_out),
    .in6(or_8_out), .in7(or_7_out), .in8(or_4_out), .in9(or_3_out), .in10(or_2_out), .out(AluOp));  // open: in11, in12, in13, in14, in15, gs, en_out, en_in

  assign WriteBack = MemR;

  // Other names for the same wires on the sheet: lw = MemR; jalr = PCSignals[0]; jal = PCSignals[1];
  //   bgeu = PCSignals[2]; bltu = PCSignals[3]; bge = PCSignals[4]; blt = PCSignals[5]; bne = PCSignals[6];
  //   beq = PCSignals[7]; sw = MemW
endmodule

module PCControl (
  input  [7:0] PCSignals,
  input  A__B,
  input  A_B,
  input  A_B_u,
  output kill,
  output PC_ctrl
);

  wire and_1_out, and_2_out, and_3_out, and_4_out, and_5_out, and_6_out, not_1_out, not_2_out, not_3_out;

  and and_1 (and_1_out, PCSignals[7], A__B);
  not not_1 (not_1_out, A__B);
  and and_2 (and_2_out, PCSignals[6], not_1_out);
  and and_3 (and_3_out, PCSignals[5], A_B);
  not not_2 (not_2_out, A_B);
  and and_4 (and_4_out, PCSignals[4], not_2_out);
  or or_1 (kill, and_1_out, and_2_out, and_3_out, and_4_out, and_5_out, and_6_out, PCSignals[1], PCSignals[0]);
  and and_5 (and_5_out, PCSignals[3], A_B_u);
  not not_3 (not_3_out, A_B_u);
  and and_6 (and_6_out, PCSignals[2], not_3_out);

  assign PC_ctrl = kill;

  // Other names for the same wires on the sheet: jalr = PCSignals[0]; jal = PCSignals[1]; bgeu = PCSignals[2];
  //   bltu = PCSignals[3]; bge = PCSignals[4]; blt = PCSignals[5]; bne = PCSignals[6]; beq = PCSignals[7]
endmodule

module Forwarding (
  input  j_type,
  input  Ex_RegW,
  input  Mem_RegW,
  input  Wb_RegW,
  input  MemR,
  input  [4:0] rs1,
  input  [4:0] rs2,
  input  [4:0] Ex_rd,
  input  [4:0] Mem_rd,
  input  [4:0] Wb_rd,
  output [1:0] FwdA,
  output stall,
  output [1:0] FwdB
);

  wire and_2_out, and_3_out, and_5_out, and_6_out, comparator_1_eq, comparator_2_eq, comparator_3_eq,
       comparator_4_eq, comparator_5_eq, comparator_6_eq, comparator_7_eq, comparator_8_eq, Ex1, Ex2,
       nj_type, nor_1_out, nor_2_out, or_1_out, rs1__0, rs2__0;
  wire [1:0] priority_encoder_1_out, priority_encoder_2_out;

  Comparator #(.width(5)) comparator_1 (.a(rs1), .b(Mem_rd), .eq(comparator_1_eq));  // open: gt, lt
  Comparator #(.width(5)) comparator_2 (.a(rs1), .b(Wb_rd), .eq(comparator_2_eq));  // open: gt, lt
  not not_1 (rs1__0, comparator_3_eq);
  Comparator #(.width(5)) comparator_3 (.a(rs1), .b({5{1'b0}}), .eq(comparator_3_eq));  // open: gt, lt
  Comparator #(.width(5)) comparator_4 (.a(rs1), .b(Ex_rd), .eq(comparator_4_eq));  // open: gt, lt
  not not_2 (rs2__0, comparator_5_eq);
  Comparator #(.width(5)) comparator_5 (.a(rs2), .b({5{1'b0}}), .eq(comparator_5_eq));  // open: gt, lt
  Comparator #(.width(5)) comparator_6 (.a(rs2), .b(Ex_rd), .eq(comparator_6_eq));  // open: gt, lt
  Comparator #(.width(5)) comparator_7 (.a(rs2), .b(Mem_rd), .eq(comparator_7_eq));  // open: gt, lt
  Comparator #(.width(5)) comparator_8 (.a(rs2), .b(Wb_rd), .eq(comparator_8_eq));  // open: gt, lt
  not not_3 (nj_type, j_type);
  and and_1 (Ex1, rs1__0, comparator_4_eq, Ex_RegW, nj_type);
  and and_2 (and_2_out, rs1__0, comparator_1_eq, Mem_RegW, nj_type);
  and and_3 (and_3_out, rs1__0, comparator_2_eq, Wb_RegW, nj_type);
  and and_4 (Ex2, rs2__0, comparator_6_eq, Ex_RegW, nj_type);
  and and_5 (and_5_out, rs2__0, comparator_7_eq, Mem_RegW, nj_type);
  and and_6 (and_6_out, rs2__0, comparator_8_eq, Wb_RegW, nj_type);
  nor nor_1 (nor_1_out, Ex1, and_2_out, and_3_out);
  nor nor_2 (nor_2_out, Ex2, and_5_out, and_6_out);
  Priority_Encoder #(.select(2)) priority_encoder_1 (
    .in0(and_3_out), .in1(and_2_out), .in2(Ex1), .in3(nor_1_out), .out(priority_encoder_1_out));  // open: gs, en_out, en_in
  assign FwdA = ~priority_encoder_1_out;  // NOT_Gate not_4, 2 bits wide
  Priority_Encoder #(.select(2)) priority_encoder_2 (
    .in0(and_6_out), .in1(and_5_out), .in2(Ex2), .in3(nor_2_out), .out(priority_encoder_2_out));  // open: gs, en_out, en_in
  assign FwdB = ~priority_encoder_2_out;  // NOT_Gate not_5, 2 bits wide
  or or_1 (or_1_out, Ex1, Ex2);
  and and_7 (stall, MemR, or_1_out);

  // Other names for the same wires on the sheet: lw = MemR
endmodule
